# Fritzing sketch puzzlebox (saved by Fritzing 0.9.2b)
circuit board: 8.54159cm x 4.1647cm
breadboards: 1

parts:
  Resonator = Resonator [frequency="16 Mhz" package=THT]
  Trellis_pin_header = female alternating pin header, 4 pins [form="♀ (female)"]
  USB = USB connector [package=THT]
  atmega328p-pu = atmega328 [package=dip]

nets:
  N1: Resonator.0, atmega328p-pu.XLAT1
  GND: Resonator.GND, Trellis_pin_header.pin3, USB.GND, USB.chassis5, USB.chassis6, atmega328p-pu.GND
  N2: Resonator.pin_1, atmega328p-pu.XLAT2
  N3: Trellis_pin_header.pin1, atmega328p-pu.A4
  N4: Trellis_pin_header.pin2, atmega328p-pu.A5
  5V: Trellis_pin_header.pin4, USB.5V, atmega328p-pu.VCC, atmega328p-pu.AVCC
